// Logisim project Decoder_3to8.circ as structural Verilog: 2 circuits, main circuit main
module main (
  input  A1,
  input  A2,
  input  A0,
  output out_4,
  output out_5,
  output out_6,
  output out_7,
  output out_8,
  output out_9,
  output out_10,
  output out_11
);

  wire decoder_2to4_1_y0, decoder_2to4_1_y1, decoder_2to4_1_y2, decoder_2to4_1_y3, decoder_2to4_2_y0,
       decoder_2to4_2_y1, decoder_2to4_2_y2, decoder_2to4_2_y3;

  Decoder_2to4 decoder_2to4_1 (
    .A1(A2), .A0(A1), .Y3(decoder_2to4_1_y3), .Y2(decoder_2to4_1_y2), .Y1(decoder_2to4_1_y1),
    .Y0(decoder_2to4_1_y0));
  Decoder_2to4 decoder_2to4_2 (
    .A1(A1), .A0(A0), .Y3(decoder_2to4_2_y3), .Y2(decoder_2to4_2_y2), .Y1(decoder_2to4_2_y1),
    .Y0(decoder_2to4_2_y0));
  and Y7 (out_4, decoder_2to4_1_y3, decoder_2to4_2_y3);
  and Y6 (out_5, decoder_2to4_1_y3, decoder_2to4_2_y2);
  and Y5 (out_6, decoder_2to4_1_y2, decoder_2to4_2_y1);
  and Y4 (out_7, decoder_2to4_1_y2, decoder_2to4_2_y0);
  and Y3 (out_8, decoder_2to4_1_y1, decoder_2to4_2_y3);
  and Y2 (out_9, decoder_2to4_1_y1, decoder_2to4_2_y2);
  and Y1 (out_10, decoder_2to4_1_y0, decoder_2to4_2_y1);
  and Y0 (out_11, decoder_2to4_1_y0, decoder_2to4_2_y0);
endmodule

module Decoder_2to4 (
  input  A1,
  input  A0,
  output Y3,
  output Y2,
  output Y1,
  output Y0
);

  wire not_1_out, not_2_out;

  not not_1 (not_1_out, A1);
  not not_2 (not_2_out, A0);
  and and_1 (Y3, A1, A0);
  and and_2 (Y2, A1, not_2_out);
  and and_3 (Y1, not_1_out, A0);
  and and_4 (Y0, not_1_out, not_2_out);
endmodule
