// Logisim project Encoder_16to4.circ as structural Verilog: 7 circuits, main circuit main
module main (
);

  wire a_out, b_out, c_out, d_out, decoder_4to16_1_y0, decoder_4to16_1_y1, decoder_4to16_1_y2,
       decoder_4to16_1_y3, decoder_4to16_1_y4, decoder_4to16_1_y5, decoder_4to16_1_y6, decoder_4to16_1_y7,
       decoder_4to16_1_y8, decoder_4to16_1_y9, decoder_4to16_1_y10, decoder_4to16_1_y11, decoder_4to16_1_y12,
       decoder_4to16_1_y13, decoder_4to16_1_y14, decoder_4to16_1_y15, dipswitch_1_p1, dipswitch_1_p2,
       dipswitch_1_p3, dipswitch_1_p4, dipswitch_1_p5, dipswitch_1_p6, dipswitch_1_p7, dipswitch_1_p8,
       dipswitch_1_p9, dipswitch_1_p10, dipswitch_1_p11, dipswitch_1_p12, dipswitch_1_p13, dipswitch_1_p14,
       dipswitch_1_p15, dipswitch_1_p16, e_out, f_out, g_out, Y0_out, Y1_out, Y2_out, Y3_out;

  // DipSwitch #(.number(16)) dipswitch_1: pin names not known; wires that end beside it: dipswitch_1_p1, dipswitch_1_p2, dipswitch_1_p3, dipswitch_1_p4, dipswitch_1_p5, dipswitch_1_p6, dipswitch_1_p7, dipswitch_1_p8, dipswitch_1_p9, dipswitch_1_p10, dipswitch_1_p11, dipswitch_1_p12, dipswitch_1_p13, dipswitch_1_p14, dipswitch_1_p15, dipswitch_1_p16
  or Y3 (Y3_out, dipswitch_1_p16, dipswitch_1_p15, dipswitch_1_p14, dipswitch_1_p13, dipswitch_1_p12, dipswitch_1_p11, dipswitch_1_p10, dipswitch_1_p9);
  or Y2 (Y2_out, dipswitch_1_p16, dipswitch_1_p15, dipswitch_1_p14, dipswitch_1_p13, dipswitch_1_p8, dipswitch_1_p7, dipswitch_1_p6, dipswitch_1_p5);
  or Y1 (Y1_out, dipswitch_1_p16, dipswitch_1_p15, dipswitch_1_p12, dipswitch_1_p11, dipswitch_1_p8, dipswitch_1_p7, dipswitch_1_p4, dipswitch_1_p3);
  or Y0 (Y0_out, dipswitch_1_p16, dipswitch_1_p14, dipswitch_1_p12, dipswitch_1_p10, dipswitch_1_p8, dipswitch_1_p6, dipswitch_1_p4, dipswitch_1_p2);
  Decoder_4to16 decoder_4to16_1 (
    .A3(Y3_out), .A2(Y2_out), .A1(Y1_out), .A0(Y0_out), .Y15(decoder_4to16_1_y15), .Y14(decoder_4to16_1_y14),
    .Y13(decoder_4to16_1_y13), .Y12(decoder_4to16_1_y12), .Y11(decoder_4to16_1_y11),
    .Y10(decoder_4to16_1_y10), .Y9(decoder_4to16_1_y9), .Y8(decoder_4to16_1_y8), .Y7(decoder_4to16_1_y7),
    .Y6(decoder_4to16_1_y6), .Y5(decoder_4to16_1_y5), .Y4(decoder_4to16_1_y4), .Y3(decoder_4to16_1_y3),
    .Y2(decoder_4to16_1_y2), .Y1(decoder_4to16_1_y1), .Y0(decoder_4to16_1_y0));
  or g (g_out, decoder_4to16_1_y15, decoder_4to16_1_y14, decoder_4to16_1_y13, decoder_4to16_1_y11, decoder_4to16_1_y10, decoder_4to16_1_y9, decoder_4to16_1_y8, decoder_4to16_1_y6, decoder_4to16_1_y5, decoder_4to16_1_y4, decoder_4to16_1_y3, decoder_4to16_1_y2);
  or f (f_out, decoder_4to16_1_y15, decoder_4to16_1_y14, decoder_4to16_1_y12, decoder_4to16_1_y11, decoder_4to16_1_y10, decoder_4to16_1_y9, decoder_4to16_1_y8, decoder_4to16_1_y6, decoder_4to16_1_y5, decoder_4to16_1_y4, decoder_4to16_1_y0);
  or e (e_out, decoder_4to16_1_y15, decoder_4to16_1_y14, decoder_4to16_1_y13, decoder_4to16_1_y12, decoder_4to16_1_y11, decoder_4to16_1_y10, decoder_4to16_1_y8, decoder_4to16_1_y6, decoder_4to16_1_y2, decoder_4to16_1_y0);
  or d (d_out, decoder_4to16_1_y14, decoder_4to16_1_y13, decoder_4to16_1_y12, decoder_4to16_1_y11, decoder_4to16_1_y9, decoder_4to16_1_y8, decoder_4to16_1_y6, decoder_4to16_1_y5, decoder_4to16_1_y3, decoder_4to16_1_y2, decoder_4to16_1_y0);
  or c (c_out, decoder_4to16_1_y10, decoder_4to16_1_y13, decoder_4to16_1_y11, decoder_4to16_1_y9, decoder_4to16_1_y8, decoder_4to16_1_y7, decoder_4to16_1_y5, decoder_4to16_1_y4, decoder_4to16_1_y3, decoder_4to16_1_y1, decoder_4to16_1_y0, decoder_4to16_1_y6);
  or b (b_out, decoder_4to16_1_y13, decoder_4to16_1_y10, decoder_4to16_1_y9, decoder_4to16_1_y8, decoder_4to16_1_y7, decoder_4to16_1_y4, decoder_4to16_1_y3, decoder_4to16_1_y2, decoder_4to16_1_y1, decoder_4to16_1_y0);
  or a (a_out, decoder_4to16_1_y15, decoder_4to16_1_y14, decoder_4to16_1_y12, decoder_4to16_1_y10, decoder_4to16_1_y9, decoder_4to16_1_y8, decoder_4to16_1_y7, decoder_4to16_1_y6, decoder_4to16_1_y5, decoder_4to16_1_y3, decoder_4to16_1_y2, decoder_4to16_1_y0);
  _7_Segment_Display u_7_segment_display_1 (
    .g(g_out), .f(f_out), .a(a_out), .b(b_out), .e(e_out), .d(d_out), .c(c_out));  // open: dp
endmodule

module Decoder_2to4 (
  input  A1,
  input  A0,
  output Y3,
  output Y2,
  output Y1,
  output Y0
);

  wire not_1_out, not_2_out;

  not not_1 (not_1_out, A1);
  not not_2 (not_2_out, A0);
  and and_1 (Y3, A1, A0);
  and and_2 (Y2, A1, not_2_out);
  and and_3 (Y1, not_1_out, A0);
  and and_4 (Y0, not_1_out, not_2_out);
endmodule

module Decoder_3to8 (
  input  A2,
  input  A1,
  input  A0,
  output Y7,
  output Y6,
  output Y5,
  output Y4,
  output Y3,
  output Y2,
  output Y1,
  output Y0
);

  wire decoder_2to4_1_y0, decoder_2to4_1_y1, decoder_2to4_1_y2, decoder_2to4_1_y3, decoder_2to4_2_y0,
       decoder_2to4_2_y1, decoder_2to4_2_y2, decoder_2to4_2_y3;

  Decoder_2to4 decoder_2to4_1 (
    .A1(A2), .A0(A1), .Y3(decoder_2to4_1_y3), .Y2(decoder_2to4_1_y2), .Y1(decoder_2to4_1_y1),
    .Y0(decoder_2to4_1_y0));
  Decoder_2to4 decoder_2to4_2 (
    .A1(A1), .A0(A0), .Y3(decoder_2to4_2_y3), .Y2(decoder_2to4_2_y2), .Y1(decoder_2to4_2_y1),
    .Y0(decoder_2to4_2_y0));
  and and_1 (Y7, decoder_2to4_1_y3, decoder_2to4_2_y3);
  and and_2 (Y6, decoder_2to4_1_y3, decoder_2to4_2_y2);
  and and_3 (Y5, decoder_2to4_1_y2, decoder_2to4_2_y1);
  and and_4 (Y4, decoder_2to4_1_y2, decoder_2to4_2_y0);
  and and_5 (Y3, decoder_2to4_1_y1, decoder_2to4_2_y3);
  and and_6 (Y2, decoder_2to4_1_y1, decoder_2to4_2_y2);
  and and_7 (Y1, decoder_2to4_1_y0, decoder_2to4_2_y1);
  and and_8 (Y0, decoder_2to4_1_y0, decoder_2to4_2_y0);
endmodule

module Decoder_4to16 (
  input  A3,
  input  A2,
  input  A1,
  input  A0,
  output Y15,
  output Y14,
  output Y13,
  output Y12,
  output Y11,
  output Y10,
  output Y9,
  output Y8,
  output Y7,
  output Y6,
  output Y5,
  output Y4,
  output Y3,
  output Y2,
  output Y1,
  output Y0
);

  wire decoder_2to4_1_y0, decoder_2to4_1_y1, decoder_2to4_1_y2, decoder_2to4_1_y3, decoder_3to8_1_y0,
       decoder_3to8_1_y1, decoder_3to8_1_y2, decoder_3to8_1_y3, decoder_3to8_1_y4, decoder_3to8_1_y5,
       decoder_3to8_1_y6, decoder_3to8_1_y7;

  Decoder_2to4 decoder_2to4_1 (
    .A1(A3), .A0(A2), .Y3(decoder_2to4_1_y3), .Y2(decoder_2to4_1_y2), .Y1(decoder_2to4_1_y1),
    .Y0(decoder_2to4_1_y0));
  Decoder_3to8 decoder_3to8_1 (
    .A2(A2), .A1(A1), .A0(A0), .Y7(decoder_3to8_1_y7), .Y6(decoder_3to8_1_y6), .Y5(decoder_3to8_1_y5),
    .Y4(decoder_3to8_1_y4), .Y3(decoder_3to8_1_y3), .Y2(decoder_3to8_1_y2), .Y1(decoder_3to8_1_y1),
    .Y0(decoder_3to8_1_y0));
  and and_1 (Y15, decoder_2to4_1_y3, decoder_3to8_1_y7);
  and and_2 (Y14, decoder_2to4_1_y3, decoder_3to8_1_y6);
  and and_3 (Y13, decoder_2to4_1_y3, decoder_3to8_1_y5);
  and and_4 (Y12, decoder_2to4_1_y3, decoder_3to8_1_y4);
  and and_5 (Y11, decoder_2to4_1_y2, decoder_3to8_1_y3);
  and and_6 (Y10, decoder_2to4_1_y2, decoder_3to8_1_y2);
  and and_7 (Y9, decoder_2to4_1_y2, decoder_3to8_1_y1);
  and and_8 (Y8, decoder_2to4_1_y2, decoder_3to8_1_y0);
  and and_9 (Y7, decoder_2to4_1_y1, decoder_3to8_1_y7);
  and and_10 (Y6, decoder_2to4_1_y1, decoder_3to8_1_y6);
  and and_11 (Y5, decoder_2to4_1_y1, decoder_3to8_1_y5);
  and and_12 (Y4, decoder_2to4_1_y1, decoder_3to8_1_y4);
  and and_13 (Y3, decoder_2to4_1_y0, decoder_3to8_1_y3);
  and and_14 (Y2, decoder_2to4_1_y0, decoder_3to8_1_y2);
  and and_15 (Y1, decoder_2to4_1_y0, decoder_3to8_1_y1);
  and and_16 (Y0, decoder_2to4_1_y0, decoder_3to8_1_y0);
endmodule

module Segement_7 (
  input  A3,
  input  A2,
  input  A1,
  input  A0
);

  wire a_out, b_out, c_out, d_out, decoder_4to16_1_y0, decoder_4to16_1_y1, decoder_4to16_1_y2,
       decoder_4to16_1_y3, decoder_4to16_1_y4, decoder_4to16_1_y5, decoder_4to16_1_y6, decoder_4to16_1_y7,
       decoder_4to16_1_y8, decoder_4to16_1_y9, decoder_4to16_1_y10, decoder_4to16_1_y11, decoder_4to16_1_y12,
       decoder_4to16_1_y13, decoder_4to16_1_y14, decoder_4to16_1_y15, e_out, f_out, g_out, h_out;

  Decoder_4to16 decoder_4to16_1 (
    .A3(A3), .A2(A2), .A1(A1), .A0(A0), .Y15(decoder_4to16_1_y15), .Y14(decoder_4to16_1_y14),
    .Y13(decoder_4to16_1_y13), .Y12(decoder_4to16_1_y12), .Y11(decoder_4to16_1_y11),
    .Y10(decoder_4to16_1_y10), .Y9(decoder_4to16_1_y9), .Y8(decoder_4to16_1_y8), .Y7(decoder_4to16_1_y7),
    .Y6(decoder_4to16_1_y6), .Y5(decoder_4to16_1_y5), .Y4(decoder_4to16_1_y4), .Y3(decoder_4to16_1_y3),
    .Y2(decoder_4to16_1_y2), .Y1(decoder_4to16_1_y1), .Y0(decoder_4to16_1_y0));
  or h (h_out, decoder_4to16_1_y15, decoder_4to16_1_y11, decoder_4to16_1_y14, decoder_4to16_1_y12, decoder_4to16_1_y10, decoder_4to16_1_y13);
  or g (g_out, decoder_4to16_1_y9, decoder_4to16_1_y6, decoder_4to16_1_y5, decoder_4to16_1_y4, decoder_4to16_1_y3, decoder_4to16_1_y2, decoder_4to16_1_y8);
  or f (f_out, decoder_4to16_1_y9, decoder_4to16_1_y8, decoder_4to16_1_y6, decoder_4to16_1_y5, decoder_4to16_1_y4, decoder_4to16_1_y0);
  or e (e_out, decoder_4to16_1_y8, decoder_4to16_1_y6, decoder_4to16_1_y2, decoder_4to16_1_y0);
  or d (d_out, decoder_4to16_1_y9, decoder_4to16_1_y8, decoder_4to16_1_y6, decoder_4to16_1_y5, decoder_4to16_1_y3, decoder_4to16_1_y2, decoder_4to16_1_y0);
  or c (c_out, decoder_4to16_1_y9, decoder_4to16_1_y8, decoder_4to16_1_y7, decoder_4to16_1_y6, decoder_4to16_1_y5, decoder_4to16_1_y4, decoder_4to16_1_y3, decoder_4to16_1_y1, decoder_4to16_1_y0);
  or b (b_out, decoder_4to16_1_y4, decoder_4to16_1_y9, decoder_4to16_1_y8, decoder_4to16_1_y7, decoder_4to16_1_y1, decoder_4to16_1_y3, decoder_4to16_1_y2, decoder_4to16_1_y0);
  or a (a_out, decoder_4to16_1_y5, decoder_4to16_1_y9, decoder_4to16_1_y8, decoder_4to16_1_y7, decoder_4to16_1_y6, decoder_4to16_1_y2, decoder_4to16_1_y0, decoder_4to16_1_y3);
  _7_Segment_Display u_7_segment_display_1 (
    .g(g_out), .f(f_out), .a(a_out), .b(b_out), .e(e_out), .d(d_out), .c(c_out), .dp(h_out));
endmodule

module Segement_7_0x (
  input  A3,
  input  A2,
  input  A1,
  input  A0
);

  wire a_out, b_out, c_out, d_out, decoder_4to16_1_y0, decoder_4to16_1_y1, decoder_4to16_1_y2,
       decoder_4to16_1_y3, decoder_4to16_1_y4, decoder_4to16_1_y5, decoder_4to16_1_y6, decoder_4to16_1_y7,
       decoder_4to16_1_y8, decoder_4to16_1_y9, decoder_4to16_1_y10, decoder_4to16_1_y11, decoder_4to16_1_y12,
       decoder_4to16_1_y13, decoder_4to16_1_y14, decoder_4to16_1_y15, e_out, f_out, g_out;

  Decoder_4to16 decoder_4to16_1 (
    .A3(A3), .A2(A2), .A1(A1), .A0(A0), .Y15(decoder_4to16_1_y15), .Y14(decoder_4to16_1_y14),
    .Y13(decoder_4to16_1_y13), .Y12(decoder_4to16_1_y12), .Y11(decoder_4to16_1_y11),
    .Y10(decoder_4to16_1_y10), .Y9(decoder_4to16_1_y9), .Y8(decoder_4to16_1_y8), .Y7(decoder_4to16_1_y7),
    .Y6(decoder_4to16_1_y6), .Y5(decoder_4to16_1_y5), .Y4(decoder_4to16_1_y4), .Y3(decoder_4to16_1_y3),
    .Y2(decoder_4to16_1_y2), .Y1(decoder_4to16_1_y1), .Y0(decoder_4to16_1_y0));
  or g (g_out, decoder_4to16_1_y15, decoder_4to16_1_y14, decoder_4to16_1_y13, decoder_4to16_1_y11, decoder_4to16_1_y10, decoder_4to16_1_y9, decoder_4to16_1_y8, decoder_4to16_1_y6, decoder_4to16_1_y5, decoder_4to16_1_y4, decoder_4to16_1_y3, decoder_4to16_1_y2);
  or f (f_out, decoder_4to16_1_y15, decoder_4to16_1_y14, decoder_4to16_1_y12, decoder_4to16_1_y11, decoder_4to16_1_y10, decoder_4to16_1_y9, decoder_4to16_1_y8, decoder_4to16_1_y6, decoder_4to16_1_y5, decoder_4to16_1_y4, decoder_4to16_1_y0);
  or e (e_out, decoder_4to16_1_y15, decoder_4to16_1_y14, decoder_4to16_1_y13, decoder_4to16_1_y12, decoder_4to16_1_y11, decoder_4to16_1_y10, decoder_4to16_1_y8, decoder_4to16_1_y6, decoder_4to16_1_y2, decoder_4to16_1_y0);
  or d (d_out, decoder_4to16_1_y14, decoder_4to16_1_y13, decoder_4to16_1_y12, decoder_4to16_1_y11, decoder_4to16_1_y9, decoder_4to16_1_y8, decoder_4to16_1_y6, decoder_4to16_1_y5, decoder_4to16_1_y3, decoder_4to16_1_y2, decoder_4to16_1_y0);
  or c (c_out, decoder_4to16_1_y10, decoder_4to16_1_y13, decoder_4to16_1_y11, decoder_4to16_1_y9, decoder_4to16_1_y8, decoder_4to16_1_y7, decoder_4to16_1_y5, decoder_4to16_1_y4, decoder_4to16_1_y3, decoder_4to16_1_y1, decoder_4to16_1_y0, decoder_4to16_1_y6);
  or b (b_out, decoder_4to16_1_y13, decoder_4to16_1_y10, decoder_4to16_1_y9, decoder_4to16_1_y8, decoder_4to16_1_y7, decoder_4to16_1_y4, decoder_4to16_1_y3, decoder_4to16_1_y2, decoder_4to16_1_y1, decoder_4to16_1_y0);
  or a (a_out, decoder_4to16_1_y15, decoder_4to16_1_y14, decoder_4to16_1_y12, decoder_4to16_1_y10, decoder_4to16_1_y9, decoder_4to16_1_y8, decoder_4to16_1_y7, decoder_4to16_1_y6, decoder_4to16_1_y5, decoder_4to16_1_y3, decoder_4to16_1_y2, decoder_4to16_1_y0);
  _7_Segment_Display u_7_segment_display_1 (
    .g(g_out), .f(f_out), .a(a_out), .b(b_out), .e(e_out), .d(d_out), .c(c_out));  // open: dp
endmodule

module Encoder_16to4 (
);

  wire dipswitch_1_p1, dipswitch_1_p2, dipswitch_1_p3, dipswitch_1_p4, dipswitch_1_p5, dipswitch_1_p6,
       dipswitch_1_p7, dipswitch_1_p8, dipswitch_1_p9, dipswitch_1_p10, dipswitch_1_p11, dipswitch_1_p12,
       dipswitch_1_p13, dipswitch_1_p14, dipswitch_1_p15, dipswitch_1_p16;

  // DipSwitch #(.number(16)) dipswitch_1: pin names not known; wires that end beside it: dipswitch_1_p1, dipswitch_1_p2, dipswitch_1_p3, dipswitch_1_p4, dipswitch_1_p5, dipswitch_1_p6, dipswitch_1_p7, dipswitch_1_p8, dipswitch_1_p9, dipswitch_1_p10, dipswitch_1_p11, dipswitch_1_p12, dipswitch_1_p13, dipswitch_1_p14, dipswitch_1_p15, dipswitch_1_p16
  // OR_Gate Y3 has open pins: in0=dipswitch_1_p16, in1=dipswitch_1_p15, in2=dipswitch_1_p14, in3=dipswitch_1_p13, in4=dipswitch_1_p12, in5=dipswitch_1_p11, in6=dipswitch_1_p10, in7=dipswitch_1_p9, out=open
  // OR_Gate Y2 has open pins: in0=dipswitch_1_p16, in1=dipswitch_1_p15, in2=dipswitch_1_p14, in3=dipswitch_1_p13, in4=dipswitch_1_p8, in5=dipswitch_1_p7, in6=dipswitch_1_p6, in7=dipswitch_1_p5, out=open
  // OR_Gate Y1 has open pins: in0=dipswitch_1_p16, in1=dipswitch_1_p15, in2=dipswitch_1_p12, in3=dipswitch_1_p11, in4=dipswitch_1_p8, in5=dipswitch_1_p7, in6=dipswitch_1_p4, in7=dipswitch_1_p3, out=open
  // OR_Gate Y0 has open pins: in0=dipswitch_1_p16, in1=dipswitch_1_p14, in2=dipswitch_1_p12, in3=dipswitch_1_p10, in4=dipswitch_1_p8, in5=dipswitch_1_p6, in6=dipswitch_1_p4, in7=dipswitch_1_p2, out=open
endmodule
