// Logisim project Adder_one_complement_4bits.circ as structural Verilog: 20 circuits, main circuit main
module main (
  input  X1,
  input  B2,
  input  B1,
  input  B0,
  input  X0,
  input  A2,
  input  A1,
  input  A0,
  output X,
  output Z2,
  output Z1,
  output Z0
);

  wire adder_sign_magnitude_4bits_1_z0, adder_sign_magnitude_4bits_1_z1, adder_sign_magnitude_4bits_1_z2,
       not_1_out, not_2_out, not_3_out, not_4_out, not_5_out, not_6_out, not_7_out, not_8_out, not_9_out,
       selector_1bit_2to1_1_d, selector_1bit_2to1_2_d, selector_1bit_2to1_3_d, selector_1bit_2to1_4_d,
       selector_1bit_2to1_5_d, selector_1bit_2to1_6_d;

  not not_1 (not_1_out, B2);
  not not_2 (not_2_out, B1);
  not not_3 (not_3_out, B0);
  not not_4 (not_4_out, A2);
  not not_5 (not_5_out, A1);
  not not_6 (not_6_out, A0);
  Selector_1bit_2to1 selector_1bit_2to1_1 (.Control(X1), .D1(not_1_out), .D0(B2), .D(selector_1bit_2to1_1_d));
  Selector_1bit_2to1 selector_1bit_2to1_2 (.Control(X1), .D1(not_2_out), .D0(B1), .D(selector_1bit_2to1_2_d));
  Selector_1bit_2to1 selector_1bit_2to1_3 (.Control(X1), .D1(not_3_out), .D0(B0), .D(selector_1bit_2to1_3_d));
  Selector_1bit_2to1 selector_1bit_2to1_4 (.Control(X0), .D1(not_4_out), .D0(A2), .D(selector_1bit_2to1_4_d));
  Selector_1bit_2to1 selector_1bit_2to1_5 (.Control(X0), .D1(not_5_out), .D0(A1), .D(selector_1bit_2to1_5_d));
  Selector_1bit_2to1 selector_1bit_2to1_6 (.Control(X0), .D1(not_6_out), .D0(A0), .D(selector_1bit_2to1_6_d));
  Adder_sign_magnitude_4bits adder_sign_magnitude_4bits_1 (
    .B2(selector_1bit_2to1_1_d), .B1(selector_1bit_2to1_2_d), .B0(selector_1bit_2to1_3_d),
    .A2(selector_1bit_2to1_4_d), .A1(selector_1bit_2to1_5_d), .A0(selector_1bit_2to1_6_d), .X1(X1), .X0(X0),
    .X(X), .Z2(adder_sign_magnitude_4bits_1_z2), .Z1(adder_sign_magnitude_4bits_1_z1),
    .Z0(adder_sign_magnitude_4bits_1_z0));  // open: B3, A3, Z3
  not not_7 (not_7_out, adder_sign_magnitude_4bits_1_z2);
  not not_8 (not_8_out, adder_sign_magnitude_4bits_1_z1);
  not not_9 (not_9_out, adder_sign_magnitude_4bits_1_z0);
  Selector_1bit_2to1 selector_1bit_2to1_7 (.Control(X), .D1(not_7_out), .D0(adder_sign_magnitude_4bits_1_z2), .D(Z2));
  Selector_1bit_2to1 selector_1bit_2to1_8 (.Control(X), .D1(not_8_out), .D0(adder_sign_magnitude_4bits_1_z1), .D(Z1));
  Selector_1bit_2to1 selector_1bit_2to1_9 (.Control(X), .D1(not_9_out), .D0(adder_sign_magnitude_4bits_1_z0), .D(Z0));
endmodule

module Decoder_2to4 (
  input  A1,
  input  A0,
  output Y3,
  output Y2,
  output Y1,
  output Y0
);

  wire not_1_out, not_2_out;

  not not_1 (not_1_out, A1);
  not not_2 (not_2_out, A0);
  and and_1 (Y3, A1, A0);
  and and_2 (Y2, A1, not_2_out);
  and and_3 (Y1, not_1_out, A0);
  and and_4 (Y0, not_1_out, not_2_out);
endmodule

module Decoder_3to8 (
  input  A2,
  input  A1,
  input  A0,
  output Y7,
  output Y6,
  output Y5,
  output Y4,
  output Y3,
  output Y2,
  output Y1,
  output Y0
);

  wire decoder_2to4_1_y0, decoder_2to4_1_y1, decoder_2to4_1_y2, decoder_2to4_1_y3, decoder_2to4_2_y0,
       decoder_2to4_2_y1, decoder_2to4_2_y2, decoder_2to4_2_y3;

  Decoder_2to4 decoder_2to4_1 (
    .A1(A2), .A0(A1), .Y3(decoder_2to4_1_y3), .Y2(decoder_2to4_1_y2), .Y1(decoder_2to4_1_y1),
    .Y0(decoder_2to4_1_y0));
  Decoder_2to4 decoder_2to4_2 (
    .A1(A1), .A0(A0), .Y3(decoder_2to4_2_y3), .Y2(decoder_2to4_2_y2), .Y1(decoder_2to4_2_y1),
    .Y0(decoder_2to4_2_y0));
  and and_1 (Y7, decoder_2to4_1_y3, decoder_2to4_2_y3);
  and and_2 (Y6, decoder_2to4_1_y3, decoder_2to4_2_y2);
  and and_3 (Y5, decoder_2to4_1_y2, decoder_2to4_2_y1);
  and and_4 (Y4, decoder_2to4_1_y2, decoder_2to4_2_y0);
  and and_5 (Y3, decoder_2to4_1_y1, decoder_2to4_2_y3);
  and and_6 (Y2, decoder_2to4_1_y1, decoder_2to4_2_y2);
  and and_7 (Y1, decoder_2to4_1_y0, decoder_2to4_2_y1);
  and and_8 (Y0, decoder_2to4_1_y0, decoder_2to4_2_y0);
endmodule

module Decoder_4to16 (
  input  A3,
  input  A2,
  input  A1,
  input  A0,
  output Y15,
  output Y14,
  output Y13,
  output Y12,
  output Y11,
  output Y10,
  output Y9,
  output Y8,
  output Y7,
  output Y6,
  output Y5,
  output Y4,
  output Y3,
  output Y2,
  output Y1,
  output Y0
);

  wire decoder_2to4_1_y0, decoder_2to4_1_y1, decoder_2to4_1_y2, decoder_2to4_1_y3, decoder_3to8_1_y0,
       decoder_3to8_1_y1, decoder_3to8_1_y2, decoder_3to8_1_y3, decoder_3to8_1_y4, decoder_3to8_1_y5,
       decoder_3to8_1_y6, decoder_3to8_1_y7;

  Decoder_2to4 decoder_2to4_1 (
    .A1(A3), .A0(A2), .Y3(decoder_2to4_1_y3), .Y2(decoder_2to4_1_y2), .Y1(decoder_2to4_1_y1),
    .Y0(decoder_2to4_1_y0));
  Decoder_3to8 decoder_3to8_1 (
    .A2(A2), .A1(A1), .A0(A0), .Y7(decoder_3to8_1_y7), .Y6(decoder_3to8_1_y6), .Y5(decoder_3to8_1_y5),
    .Y4(decoder_3to8_1_y4), .Y3(decoder_3to8_1_y3), .Y2(decoder_3to8_1_y2), .Y1(decoder_3to8_1_y1),
    .Y0(decoder_3to8_1_y0));
  and and_1 (Y15, decoder_2to4_1_y3, decoder_3to8_1_y7);
  and and_2 (Y14, decoder_2to4_1_y3, decoder_3to8_1_y6);
  and and_3 (Y13, decoder_2to4_1_y3, decoder_3to8_1_y5);
  and and_4 (Y12, decoder_2to4_1_y3, decoder_3to8_1_y4);
  and and_5 (Y11, decoder_2to4_1_y2, decoder_3to8_1_y3);
  and and_6 (Y10, decoder_2to4_1_y2, decoder_3to8_1_y2);
  and and_7 (Y9, decoder_2to4_1_y2, decoder_3to8_1_y1);
  and and_8 (Y8, decoder_2to4_1_y2, decoder_3to8_1_y0);
  and and_9 (Y7, decoder_2to4_1_y1, decoder_3to8_1_y7);
  and and_10 (Y6, decoder_2to4_1_y1, decoder_3to8_1_y6);
  and and_11 (Y5, decoder_2to4_1_y1, decoder_3to8_1_y5);
  and and_12 (Y4, decoder_2to4_1_y1, decoder_3to8_1_y4);
  and and_13 (Y3, decoder_2to4_1_y0, decoder_3to8_1_y3);
  and and_14 (Y2, decoder_2to4_1_y0, decoder_3to8_1_y2);
  and and_15 (Y1, decoder_2to4_1_y0, decoder_3to8_1_y1);
  and and_16 (Y0, decoder_2to4_1_y0, decoder_3to8_1_y0);
endmodule

module Segement_7 (
  input  A3,
  input  A2,
  input  A1,
  input  A0
);

  wire a_out, b_out, c_out, d_out, decoder_4to16_1_y0, decoder_4to16_1_y1, decoder_4to16_1_y2,
       decoder_4to16_1_y3, decoder_4to16_1_y4, decoder_4to16_1_y5, decoder_4to16_1_y6, decoder_4to16_1_y7,
       decoder_4to16_1_y8, decoder_4to16_1_y9, decoder_4to16_1_y10, decoder_4to16_1_y11, decoder_4to16_1_y12,
       decoder_4to16_1_y13, decoder_4to16_1_y14, decoder_4to16_1_y15, e_out, f_out, g_out, h_out;

  Decoder_4to16 decoder_4to16_1 (
    .A3(A3), .A2(A2), .A1(A1), .A0(A0), .Y15(decoder_4to16_1_y15), .Y14(decoder_4to16_1_y14),
    .Y13(decoder_4to16_1_y13), .Y12(decoder_4to16_1_y12), .Y11(decoder_4to16_1_y11),
    .Y10(decoder_4to16_1_y10), .Y9(decoder_4to16_1_y9), .Y8(decoder_4to16_1_y8), .Y7(decoder_4to16_1_y7),
    .Y6(decoder_4to16_1_y6), .Y5(decoder_4to16_1_y5), .Y4(decoder_4to16_1_y4), .Y3(decoder_4to16_1_y3),
    .Y2(decoder_4to16_1_y2), .Y1(decoder_4to16_1_y1), .Y0(decoder_4to16_1_y0));
  or h (h_out, decoder_4to16_1_y15, decoder_4to16_1_y11, decoder_4to16_1_y14, decoder_4to16_1_y12, decoder_4to16_1_y10, decoder_4to16_1_y13);
  or g (g_out, decoder_4to16_1_y9, decoder_4to16_1_y6, decoder_4to16_1_y5, decoder_4to16_1_y4, decoder_4to16_1_y3, decoder_4to16_1_y2, decoder_4to16_1_y8);
  or f (f_out, decoder_4to16_1_y9, decoder_4to16_1_y8, decoder_4to16_1_y6, decoder_4to16_1_y5, decoder_4to16_1_y4, decoder_4to16_1_y0);
  or e (e_out, decoder_4to16_1_y8, decoder_4to16_1_y6, decoder_4to16_1_y2, decoder_4to16_1_y0);
  or d (d_out, decoder_4to16_1_y9, decoder_4to16_1_y8, decoder_4to16_1_y6, decoder_4to16_1_y5, decoder_4to16_1_y3, decoder_4to16_1_y2, decoder_4to16_1_y0);
  or c (c_out, decoder_4to16_1_y9, decoder_4to16_1_y8, decoder_4to16_1_y7, decoder_4to16_1_y6, decoder_4to16_1_y5, decoder_4to16_1_y4, decoder_4to16_1_y3, decoder_4to16_1_y1, decoder_4to16_1_y0);
  or b (b_out, decoder_4to16_1_y4, decoder_4to16_1_y9, decoder_4to16_1_y8, decoder_4to16_1_y7, decoder_4to16_1_y1, decoder_4to16_1_y3, decoder_4to16_1_y2, decoder_4to16_1_y0);
  or a (a_out, decoder_4to16_1_y5, decoder_4to16_1_y9, decoder_4to16_1_y8, decoder_4to16_1_y7, decoder_4to16_1_y6, decoder_4to16_1_y2, decoder_4to16_1_y0, decoder_4to16_1_y3);
  _7_Segment_Display u_7_segment_display_1 (
    .g(g_out), .f(f_out), .a(a_out), .b(b_out), .e(e_out), .d(d_out), .c(c_out), .dp(h_out));
endmodule

module Segement_7_0x (
  input  A3,
  input  A2,
  input  A1,
  input  A0,
  output g,
  output f,
  output e,
  output d,
  output c,
  output b,
  output a
);

  wire decoder_4to16_1_y0, decoder_4to16_1_y1, decoder_4to16_1_y2, decoder_4to16_1_y3, decoder_4to16_1_y4,
       decoder_4to16_1_y5, decoder_4to16_1_y6, decoder_4to16_1_y7, decoder_4to16_1_y8, decoder_4to16_1_y9,
       decoder_4to16_1_y10, decoder_4to16_1_y11, decoder_4to16_1_y12, decoder_4to16_1_y13,
       decoder_4to16_1_y14, decoder_4to16_1_y15;

  Decoder_4to16 decoder_4to16_1 (
    .A3(A3), .A2(A2), .A1(A1), .A0(A0), .Y15(decoder_4to16_1_y15), .Y14(decoder_4to16_1_y14),
    .Y13(decoder_4to16_1_y13), .Y12(decoder_4to16_1_y12), .Y11(decoder_4to16_1_y11),
    .Y10(decoder_4to16_1_y10), .Y9(decoder_4to16_1_y9), .Y8(decoder_4to16_1_y8), .Y7(decoder_4to16_1_y7),
    .Y6(decoder_4to16_1_y6), .Y5(decoder_4to16_1_y5), .Y4(decoder_4to16_1_y4), .Y3(decoder_4to16_1_y3),
    .Y2(decoder_4to16_1_y2), .Y1(decoder_4to16_1_y1), .Y0(decoder_4to16_1_y0));
  or or_1 (g, decoder_4to16_1_y15, decoder_4to16_1_y14, decoder_4to16_1_y13, decoder_4to16_1_y11, decoder_4to16_1_y10, decoder_4to16_1_y9, decoder_4to16_1_y8, decoder_4to16_1_y6, decoder_4to16_1_y5, decoder_4to16_1_y4, decoder_4to16_1_y3, decoder_4to16_1_y2);
  or or_2 (f, decoder_4to16_1_y15, decoder_4to16_1_y14, decoder_4to16_1_y12, decoder_4to16_1_y11, decoder_4to16_1_y10, decoder_4to16_1_y9, decoder_4to16_1_y8, decoder_4to16_1_y6, decoder_4to16_1_y5, decoder_4to16_1_y4, decoder_4to16_1_y0);
  or or_3 (e, decoder_4to16_1_y15, decoder_4to16_1_y14, decoder_4to16_1_y13, decoder_4to16_1_y12, decoder_4to16_1_y11, decoder_4to16_1_y10, decoder_4to16_1_y8, decoder_4to16_1_y6, decoder_4to16_1_y2, decoder_4to16_1_y0);
  or or_4 (d, decoder_4to16_1_y14, decoder_4to16_1_y13, decoder_4to16_1_y12, decoder_4to16_1_y11, decoder_4to16_1_y9, decoder_4to16_1_y8, decoder_4to16_1_y6, decoder_4to16_1_y5, decoder_4to16_1_y3, decoder_4to16_1_y2, decoder_4to16_1_y0);
  or or_5 (c, decoder_4to16_1_y10, decoder_4to16_1_y13, decoder_4to16_1_y11, decoder_4to16_1_y9, decoder_4to16_1_y8, decoder_4to16_1_y7, decoder_4to16_1_y5, decoder_4to16_1_y4, decoder_4to16_1_y3, decoder_4to16_1_y1, decoder_4to16_1_y0, decoder_4to16_1_y6);
  or or_6 (b, decoder_4to16_1_y13, decoder_4to16_1_y10, decoder_4to16_1_y9, decoder_4to16_1_y8, decoder_4to16_1_y7, decoder_4to16_1_y4, decoder_4to16_1_y3, decoder_4to16_1_y2, decoder_4to16_1_y1, decoder_4to16_1_y0);
  or or_7 (a, decoder_4to16_1_y15, decoder_4to16_1_y14, decoder_4to16_1_y12, decoder_4to16_1_y10, decoder_4to16_1_y9, decoder_4to16_1_y8, decoder_4to16_1_y7, decoder_4to16_1_y6, decoder_4to16_1_y5, decoder_4to16_1_y3, decoder_4to16_1_y2, decoder_4to16_1_y0);
endmodule

module Encoder_16to4 (
);

  wire dipswitch_1_p1, dipswitch_1_p2, dipswitch_1_p3, dipswitch_1_p4, dipswitch_1_p5, dipswitch_1_p6,
       dipswitch_1_p7, dipswitch_1_p8, dipswitch_1_p9, dipswitch_1_p10, dipswitch_1_p11, dipswitch_1_p12,
       dipswitch_1_p13, dipswitch_1_p14, dipswitch_1_p15, dipswitch_1_p16;

  // DipSwitch #(.number(16)) dipswitch_1: pin names not known; wires that end beside it: dipswitch_1_p1, dipswitch_1_p2, dipswitch_1_p3, dipswitch_1_p4, dipswitch_1_p5, dipswitch_1_p6, dipswitch_1_p7, dipswitch_1_p8, dipswitch_1_p9, dipswitch_1_p10, dipswitch_1_p11, dipswitch_1_p12, dipswitch_1_p13, dipswitch_1_p14, dipswitch_1_p15, dipswitch_1_p16
  // OR_Gate Y3 has open pins: in0=dipswitch_1_p16, in1=dipswitch_1_p15, in2=dipswitch_1_p14, in3=dipswitch_1_p13, in4=dipswitch_1_p12, in5=dipswitch_1_p11, in6=dipswitch_1_p10, in7=dipswitch_1_p9, out=open
  // OR_Gate Y2 has open pins: in0=dipswitch_1_p16, in1=dipswitch_1_p15, in2=dipswitch_1_p14, in3=dipswitch_1_p13, in4=dipswitch_1_p8, in5=dipswitch_1_p7, in6=dipswitch_1_p6, in7=dipswitch_1_p5, out=open
  // OR_Gate Y1 has open pins: in0=dipswitch_1_p16, in1=dipswitch_1_p15, in2=dipswitch_1_p12, in3=dipswitch_1_p11, in4=dipswitch_1_p8, in5=dipswitch_1_p7, in6=dipswitch_1_p4, in7=dipswitch_1_p3, out=open
  // OR_Gate Y0 has open pins: in0=dipswitch_1_p16, in1=dipswitch_1_p14, in2=dipswitch_1_p12, in3=dipswitch_1_p10, in4=dipswitch_1_p8, in5=dipswitch_1_p6, in6=dipswitch_1_p4, in7=dipswitch_1_p2, out=open
endmodule

module Encoder_4to2_priority (
  input  A3,
  input  A2,
  input  A1,
  input  A0,
  output Y2,
  output Y0,
  output X
);

  wire nor_1_out, nor_2_out, nor_3_out, not_1_out, not_2_out, not_3_out;

  nor nor_1 (nor_1_out, A3, A2);
  not not_1 (not_1_out, nor_1_out);
  nor nor_2 (nor_2_out, not_1_out, A1);
  not not_2 (not_2_out, nor_2_out);
  nor nor_3 (nor_3_out, not_1_out, nor_2_out);
  // NOR_Gate nor_4 has open pins: in0=not_2_out, in1=A0, out=open
  not not_3 (not_3_out, nor_1_out);
  and and_1 (X, ~A0, ~A1, ~A3, ~A2);  // AND_Gate
  or or_1 (Y2, A3, not_3_out);
  or or_2 (Y0, A3, nor_3_out);
endmodule

module Encoder_16to4_priority (
  input  A15,
  input  A14,
  input  A13,
  input  A12,
  input  A11,
  input  A10,
  input  A9,
  input  A8,
  input  A7,
  input  A6,
  input  A5,
  input  A4,
  input  A3,
  input  A2,
  input  A1,
  input  A0,
  output Y3,
  output Y2,
  output Y1,
  output Y0,
  output X
);

  wire and_1_out, and_2_out, and_3_out, and_4_out, and_5_out, and_6_out, and_7_out, and_8_out, and_9_out,
       and_10_out, and_11_out, and_12_out, and_13_out, and_14_out, and_15_out, and_16_out, and_17_out,
       and_18_out, and_19_out, and_20_out, and_21_out, and_22_out, and_23_out, and_24_out, and_25_out,
       and_26_out, and_27_out, and_29_out, and_30_out, and_31_out, encoder_4to2_priority_1_x,
       encoder_4to2_priority_1_y0, encoder_4to2_priority_1_y2, encoder_4to2_priority_2_x,
       encoder_4to2_priority_2_y0, encoder_4to2_priority_2_y2, encoder_4to2_priority_3_x,
       encoder_4to2_priority_3_y0, encoder_4to2_priority_3_y2, encoder_4to2_priority_4_y0,
       encoder_4to2_priority_4_y2, not_1_out, not_2_out, not_3_out;

  Encoder_4to2_priority encoder_4to2_priority_1 (
    .A3(A0), .A2(A1), .A1(A2), .A0(A3), .Y2(encoder_4to2_priority_1_y2), .Y0(encoder_4to2_priority_1_y0),
    .X(encoder_4to2_priority_1_x));
  and and_1 (and_1_out, encoder_4to2_priority_1_x, A4);
  and and_2 (and_2_out, encoder_4to2_priority_1_x, A5);
  and and_3 (and_3_out, encoder_4to2_priority_1_x, A6);
  and and_4 (and_4_out, encoder_4to2_priority_1_x, A7);
  Encoder_4to2_priority encoder_4to2_priority_2 (
    .A3(and_1_out), .A2(and_2_out), .A1(and_3_out), .A0(and_4_out), .Y2(encoder_4to2_priority_2_y2),
    .Y0(encoder_4to2_priority_2_y0), .X(encoder_4to2_priority_2_x));
  and and_5 (and_5_out, encoder_4to2_priority_2_x, encoder_4to2_priority_1_x, A8);
  and and_6 (and_6_out, encoder_4to2_priority_2_x, encoder_4to2_priority_1_x, A9);
  and and_7 (and_7_out, encoder_4to2_priority_2_x, encoder_4to2_priority_1_x, A10);
  and and_8 (and_8_out, encoder_4to2_priority_2_x, encoder_4to2_priority_1_x, A11);
  Encoder_4to2_priority encoder_4to2_priority_3 (
    .A3(and_5_out), .A2(and_6_out), .A1(and_7_out), .A0(and_8_out), .Y2(encoder_4to2_priority_3_y2),
    .Y0(encoder_4to2_priority_3_y0), .X(encoder_4to2_priority_3_x));
  and and_9 (and_9_out, encoder_4to2_priority_3_x, encoder_4to2_priority_2_x, encoder_4to2_priority_1_x, A12);
  and and_10 (and_10_out, encoder_4to2_priority_3_x, encoder_4to2_priority_2_x, encoder_4to2_priority_1_x, A13);
  and and_11 (and_11_out, encoder_4to2_priority_3_x, encoder_4to2_priority_2_x, encoder_4to2_priority_1_x, A14);
  and and_12 (and_12_out, encoder_4to2_priority_3_x, encoder_4to2_priority_2_x, encoder_4to2_priority_1_x, A15);
  not not_1 (not_1_out, encoder_4to2_priority_1_x);
  not not_2 (not_2_out, encoder_4to2_priority_2_x);
  not not_3 (not_3_out, encoder_4to2_priority_3_x);
  Encoder_4to2_priority encoder_4to2_priority_4 (
    .A3(and_9_out), .A2(and_10_out), .A1(and_11_out), .A0(and_12_out), .Y2(encoder_4to2_priority_4_y2),
    .Y0(encoder_4to2_priority_4_y0), .X(X));
  and and_13 (and_13_out, encoder_4to2_priority_1_y2, encoder_4to2_priority_1_y0);
  and and_14 (and_14_out, encoder_4to2_priority_1_y2, ~encoder_4to2_priority_1_y0);  // AND_Gate
  and and_15 (and_15_out, ~encoder_4to2_priority_1_y2, encoder_4to2_priority_1_y0);  // AND_Gate
  and and_16 (and_16_out, ~encoder_4to2_priority_1_y2, ~encoder_4to2_priority_1_y0);  // AND_Gate
  and and_17 (and_17_out, encoder_4to2_priority_2_y2, encoder_4to2_priority_2_y0);
  and and_18 (and_18_out, encoder_4to2_priority_2_y2, ~encoder_4to2_priority_2_y0);  // AND_Gate
  and and_19 (and_19_out, ~encoder_4to2_priority_2_y2, encoder_4to2_priority_2_y0);  // AND_Gate
  and and_20 (and_20_out, ~encoder_4to2_priority_2_y2, ~encoder_4to2_priority_2_y0);  // AND_Gate
  and and_21 (and_21_out, encoder_4to2_priority_3_y2, encoder_4to2_priority_3_y0);
  and and_22 (and_22_out, encoder_4to2_priority_3_y2, ~encoder_4to2_priority_3_y0);  // AND_Gate
  and and_23 (and_23_out, ~encoder_4to2_priority_3_y2, encoder_4to2_priority_3_y0);  // AND_Gate
  and and_24 (and_24_out, ~encoder_4to2_priority_3_y2, ~encoder_4to2_priority_3_y0);  // AND_Gate
  and and_25 (and_25_out, encoder_4to2_priority_4_y2, encoder_4to2_priority_4_y0);
  and and_26 (and_26_out, encoder_4to2_priority_4_y2, ~encoder_4to2_priority_4_y0);  // AND_Gate
  and and_27 (and_27_out, ~encoder_4to2_priority_4_y2, encoder_4to2_priority_4_y0);  // AND_Gate
  // AND_Gate and_28 has open pins: in0=encoder_4to2_priority_4_y2, in1=encoder_4to2_priority_4_y0, out=open
  and and_29 (and_29_out, not_1_out, and_16_out);
  and and_30 (and_30_out, not_2_out, and_20_out);
  and and_31 (and_31_out, not_3_out, and_24_out);
  or or_1 (Y3, and_13_out, and_14_out, and_15_out, and_29_out, and_17_out, and_18_out, and_19_out, and_30_out);
  or or_2 (Y2, and_13_out, and_14_out, and_15_out, and_29_out, and_21_out, and_22_out, and_23_out, and_31_out);
  or or_3 (Y1, and_13_out, and_14_out, and_17_out, and_18_out, and_21_out, and_22_out, and_25_out, and_26_out);
  or or_4 (Y0, and_13_out, and_15_out, and_17_out, and_19_out, and_21_out, and_23_out, and_25_out, and_27_out);
endmodule

module Decoder_2to1_legal (
  input  in_1,
  input  in_2,
  output Y0,
  output X
);

  wire and_1_out, and_2_out, xor_1_out;

  xor xor_1 (xor_1_out, in_1, in_2);
  and and_1 (and_1_out, in_1, xor_1_out);
  and and_2 (and_2_out, in_2, xor_1_out);
  not not_1 (X, xor_1_out);
  and and_3 (Y0, and_1_out, ~and_2_out);  // AND_Gate
endmodule

module Selector_3bits_4to1 (
  input  in_1,
  input  in_2,
  output out_3,
  output out_4,
  output out_5,
  output out_6,
  output out_7,
  output out_8,
  output out_9,
  output out_10,
  output out_11,
  output out_12,
  output out_13,
  output out_14
);

  wire and_1_out, and_2_out, and_3_out, and_4_out;

  and and_1 (and_1_out, in_1, in_2);
  and and_2 (and_2_out, in_1, ~in_2);  // AND_Gate
  and and_3 (and_3_out, ~in_1, in_2);  // AND_Gate
  and and_4 (and_4_out, ~in_1, ~in_2);  // AND_Gate
  and and_5 (out_12, and_4_out, 1'b0);
  and and_6 (out_13, and_4_out, 1'b0);
  and and_7 (out_14, and_4_out, 1'b1);
  and and_8 (out_3, and_1_out, 1'b1);
  and and_9 (out_4, and_1_out, 1'b1);
  and and_10 (out_5, and_1_out, 1'b1);
  and and_11 (out_6, and_2_out, 1'b1);
  and and_12 (out_7, and_2_out, 1'b0);
  and and_13 (out_8, and_2_out, 1'b1);
  and and_14 (out_9, and_3_out, 1'b0);
  and and_15 (out_10, and_3_out, 1'b1);
  and and_16 (out_11, and_3_out, 1'b1);
endmodule

module HA (
  input  B,
  input  A,
  output S,
  output Cout
);

  xor xor_1 (S, B, A);
  and and_1 (Cout, B, A);
endmodule

module FA (
  input  Cin,
  input  B,
  input  A,
  output S,
  output Cout
);

  wire ha_1_cout, ha_1_s, ha_2_cout;

  HA ha_1 (.B(B), .A(A), .S(ha_1_s), .Cout(ha_1_cout));
  HA ha_2 (.B(Cin), .A(ha_1_s), .S(S), .Cout(ha_2_cout));
  or or_1 (Cout, ha_2_cout, ha_1_cout);
endmodule

module FA_4bits (
  input  B0,
  input  A0,
  input  B1,
  input  A1,
  input  B2,
  input  A2,
  input  B3,
  input  A3,
  output Z3,
  output Z2,
  output Z1,
  output Z0
);

  wire fa_1_cout, fa_2_cout, fa_3_cout, fa_4_cout;

  FA fa_1 (.B(B0), .A(A0), .S(Z0), .Cout(fa_1_cout));  // open: Cin
  LED led_1 (.in(fa_1_cout));
  FA fa_2 (.Cin(fa_1_cout), .B(B1), .A(A1), .S(Z1), .Cout(fa_2_cout));
  LED led_2 (.in(fa_2_cout));
  FA fa_3 (.Cin(fa_2_cout), .B(B2), .A(A2), .S(Z2), .Cout(fa_3_cout));
  LED led_3 (.in(fa_3_cout));
  FA fa_4 (.Cin(fa_3_cout), .B(B3), .A(A3), .S(Z3), .Cout(fa_4_cout));
  LED led_4 (.in(fa_4_cout));
endmodule

module Subtractor_1bit (
  input  A,
  input  B,
  output D,
  output C
);

  wire not_1_out;

  not not_1 (not_1_out, A);
  and and_1 (D, not_1_out, B);
  xor xor_1 (C, A, B);
endmodule

module Subtractor_4bits_fool (
  input  A3,
  input  A2,
  input  A1,
  input  A0,
  input  B0,
  input  B1,
  input  B2,
  input  B3,
  output out_9,
  output out_10,
  output out_11,
  output out_12,
  output out_13
);

  wire and_1_out, and_2_out, and_3_out, and_4_out, and_5_out, and_6_out, and_7_out, and_8_out, and_9_out,
       and_10_out, and_11_out, and_12_out, segement_7_0x_1_a, segement_7_0x_1_b, segement_7_0x_1_c,
       segement_7_0x_1_d, segement_7_0x_1_e, segement_7_0x_1_f, segement_7_0x_1_g, subtractor_1bit_1_d,
       subtractor_1bit_2_d, subtractor_1bit_3_d, subtractor_1bit_4_d, xor_1_out, xor_2_out, xor_3_out,
       xor_4_out, xor_5_out, xor_6_out;

  Subtractor_1bit subtractor_1bit_1 (.A(A0), .B(B0), .D(subtractor_1bit_1_d), .C(out_13));
  xor xor_1 (xor_1_out, A1, subtractor_1bit_1_d);
  and and_1 (and_1_out, ~A1, xor_1_out);  // AND_Gate
  and and_2 (and_2_out, xor_1_out, ~and_5_out);  // AND_Gate
  and and_3 (and_3_out, ~A2, xor_2_out);  // AND_Gate
  xor xor_2 (xor_2_out, A2, and_1_out);
  and and_4 (and_4_out, xor_2_out, ~and_5_out);  // AND_Gate
  xor xor_3 (xor_3_out, A3, and_3_out);
  and and_5 (and_5_out, ~A3, xor_3_out);  // AND_Gate
  and and_6 (and_6_out, xor_3_out, ~and_5_out);  // AND_Gate
  Subtractor_1bit subtractor_1bit_2 (.A(and_2_out), .B(B1), .D(subtractor_1bit_2_d), .C(out_12));
  xor xor_4 (xor_4_out, and_4_out, subtractor_1bit_2_d);
  and and_7 (and_7_out, ~and_4_out, xor_4_out);  // AND_Gate
  and and_8 (and_8_out, xor_4_out, ~and_9_out);  // AND_Gate
  xor xor_5 (xor_5_out, and_6_out, and_7_out);
  and and_9 (and_9_out, ~and_6_out, xor_5_out);  // AND_Gate
  and and_10 (and_10_out, xor_5_out, ~and_9_out);  // AND_Gate
  Subtractor_1bit subtractor_1bit_3 (.A(and_8_out), .B(B2), .D(subtractor_1bit_3_d), .C(out_11));
  xor xor_6 (xor_6_out, and_10_out, subtractor_1bit_3_d);
  and and_11 (and_11_out, ~and_10_out, xor_6_out);  // AND_Gate
  and and_12 (and_12_out, xor_6_out, ~and_11_out);  // AND_Gate
  Subtractor_1bit subtractor_1bit_4 (.A(and_12_out), .B(B3), .D(subtractor_1bit_4_d), .C(out_10));
  or or_1 (out_9, and_5_out, and_9_out, and_11_out, subtractor_1bit_4_d);
  Segement_7_0x segement_7_0x_1 (
    .A3(out_10), .A2(out_11), .A1(out_12), .A0(out_13), .g(segement_7_0x_1_g), .f(segement_7_0x_1_f),
    .e(segement_7_0x_1_e), .d(segement_7_0x_1_d), .c(segement_7_0x_1_c), .b(segement_7_0x_1_b),
    .a(segement_7_0x_1_a));
  _7_Segment_Display u_7_segment_display_1 (
    .g(segement_7_0x_1_g), .f(segement_7_0x_1_f), .a(segement_7_0x_1_a), .b(segement_7_0x_1_b),
    .e(segement_7_0x_1_e), .d(segement_7_0x_1_d), .c(segement_7_0x_1_c));  // open: dp
endmodule

module Subtractor_1bit_nice (
  input  X,
  input  Y,
  input  Bin,
  output Bout,
  output Z
);

  wire and_1_out, and_2_out, and_3_out, or_1_out, xor_1_out;

  or or_1 (or_1_out, Bin, Y);
  xor xor_1 (xor_1_out, X, Y);
  and and_1 (and_1_out, Bin, Y);
  and and_2 (and_2_out, or_1_out, ~X);  // AND_Gate
  and and_3 (and_3_out, and_1_out, X);
  xor xor_2 (Z, xor_1_out, Bin);
  or or_2 (Bout, and_3_out, and_2_out);
endmodule

module Subtractor_4bits_nice (
  input  X3,
  input  Y3,
  input  X2,
  input  Y2,
  input  X1,
  input  Y1,
  input  X0,
  input  Y0,
  output sign,
  output Z0,
  output Z1,
  output Z2,
  output Z3
);

  wire subtractor_1bit_nice_1_bout, subtractor_1bit_nice_2_bout, subtractor_1bit_nice_3_bout;

  Subtractor_1bit_nice subtractor_1bit_nice_1 (
    .X(X0), .Y(Y0), .Bout(subtractor_1bit_nice_1_bout), .Z(Z0));  // open: Bin
  Subtractor_1bit_nice subtractor_1bit_nice_2 (
    .X(X1), .Y(Y1), .Bin(subtractor_1bit_nice_1_bout), .Bout(subtractor_1bit_nice_2_bout), .Z(Z1));
  Subtractor_1bit_nice subtractor_1bit_nice_3 (
    .X(X2), .Y(Y2), .Bin(subtractor_1bit_nice_2_bout), .Bout(subtractor_1bit_nice_3_bout), .Z(Z2));
  Subtractor_1bit_nice subtractor_1bit_nice_4 (.X(X3), .Y(Y3), .Bin(subtractor_1bit_nice_3_bout), .Bout(sign), .Z(Z3));
endmodule

module Selector_1bit_2to1 (
  input  Control,
  input  D1,
  input  D0,
  output D
);

  wire and_1_out, and_2_out;

  and and_1 (and_1_out, D1, Control);
  and and_2 (and_2_out, ~Control, D0);  // AND_Gate
  or or_1 (D, and_1_out, and_2_out);
endmodule

module Adder_sign_magnitude_4bits (
  input  B3,
  input  B2,
  input  B1,
  input  B0,
  input  A3,
  input  A2,
  input  A1,
  input  A0,
  input  X1,
  input  X0,
  output X,
  output Z3,
  output Z2,
  output Z1,
  output Z0
);

  wire and_1_out, and_2_out, and_3_out, and_4_out, and_5_out, and_6_out, and_7_out, and_8_out, and_9_out,
       and_10_out, and_11_out, and_12_out, and_13_out, and_14_out, and_15_out, and_16_out, and_17_out,
       and_18_out, and_19_out, and_20_out, and_21_out, and_22_out, and_23_out, and_24_out, and_25_out,
       fa_4bits_1_z0, fa_4bits_1_z1, fa_4bits_1_z2, fa_4bits_1_z3, selector_1bit_2to1_1_d,
       selector_1bit_2to1_3_d, selector_1bit_2to1_4_d, selector_1bit_2to1_5_d, selector_1bit_2to1_6_d,
       subtractor_4bits_nice_1_sign, subtractor_4bits_nice_1_z0, subtractor_4bits_nice_1_z1,
       subtractor_4bits_nice_1_z2, subtractor_4bits_nice_1_z3, subtractor_4bits_nice_2_z0,
       subtractor_4bits_nice_2_z1, subtractor_4bits_nice_2_z2, subtractor_4bits_nice_2_z3, xor_1_out;

  and and_1 (and_1_out, X0, ~xor_1_out);  // AND_Gate
  xor xor_1 (xor_1_out, X1, X0);
  and and_2 (and_2_out, B3, ~xor_1_out);  // AND_Gate
  and and_3 (and_3_out, B2, ~xor_1_out);  // AND_Gate
  and and_4 (and_4_out, B1, ~xor_1_out);  // AND_Gate
  and and_5 (and_5_out, B0, ~xor_1_out);  // AND_Gate
  and and_6 (and_6_out, A3, ~xor_1_out);  // AND_Gate
  and and_7 (and_7_out, A2, ~xor_1_out);  // AND_Gate
  and and_8 (and_8_out, A1, ~xor_1_out);  // AND_Gate
  and and_9 (and_9_out, A0, ~xor_1_out);  // AND_Gate
  and and_10 (and_10_out, B3, xor_1_out);
  and and_11 (and_11_out, B2, xor_1_out);
  and and_12 (and_12_out, B1, xor_1_out);
  and and_13 (and_13_out, B0, xor_1_out);
  and and_14 (and_14_out, A3, xor_1_out);
  and and_15 (and_15_out, A2, xor_1_out);
  and and_16 (and_16_out, A1, xor_1_out);
  and and_17 (and_17_out, A0, xor_1_out);
  FA_4bits fa_4bits_1 (
    .B0(and_5_out), .A0(and_9_out), .B1(and_4_out), .A1(and_8_out), .B2(and_3_out), .A2(and_7_out),
    .B3(and_2_out), .A3(and_6_out), .Z3(fa_4bits_1_z3), .Z2(fa_4bits_1_z2), .Z1(fa_4bits_1_z1),
    .Z0(fa_4bits_1_z0));
  Subtractor_4bits_nice subtractor_4bits_nice_1 (
    .X3(and_10_out), .Y3(and_14_out), .X2(and_11_out), .Y2(and_15_out), .X1(and_12_out), .Y1(and_16_out),
    .X0(and_13_out), .Y0(and_17_out), .sign(subtractor_4bits_nice_1_sign), .Z0(subtractor_4bits_nice_1_z0),
    .Z1(subtractor_4bits_nice_1_z1), .Z2(subtractor_4bits_nice_1_z2), .Z3(subtractor_4bits_nice_1_z3));
  and and_18 (and_18_out, subtractor_4bits_nice_1_sign, and_14_out);
  and and_19 (and_19_out, subtractor_4bits_nice_1_sign, and_15_out);
  and and_20 (and_20_out, subtractor_4bits_nice_1_sign, and_16_out);
  and and_21 (and_21_out, subtractor_4bits_nice_1_sign, and_17_out);
  and and_22 (and_22_out, subtractor_4bits_nice_1_sign, and_10_out);
  and and_23 (and_23_out, subtractor_4bits_nice_1_sign, and_11_out);
  and and_24 (and_24_out, subtractor_4bits_nice_1_sign, and_12_out);
  and and_25 (and_25_out, subtractor_4bits_nice_1_sign, and_13_out);
  Selector_1bit_2to1 selector_1bit_2to1_1 (
    .Control(subtractor_4bits_nice_1_sign), .D1(X0), .D0(X1), .D(selector_1bit_2to1_1_d));
  Subtractor_4bits_nice subtractor_4bits_nice_2 (
    .X3(and_18_out), .Y3(and_22_out), .X2(and_19_out), .Y2(and_23_out), .X1(and_20_out), .Y1(and_24_out),
    .X0(and_21_out), .Y0(and_25_out), .Z0(subtractor_4bits_nice_2_z0), .Z1(subtractor_4bits_nice_2_z1),
    .Z2(subtractor_4bits_nice_2_z2), .Z3(subtractor_4bits_nice_2_z3));  // open: sign
  Selector_1bit_2to1 selector_1bit_2to1_2 (.Control(xor_1_out), .D1(selector_1bit_2to1_1_d), .D0(and_1_out), .D(X));
  Selector_1bit_2to1 selector_1bit_2to1_3 (
    .Control(subtractor_4bits_nice_1_sign), .D1(subtractor_4bits_nice_2_z3), .D0(subtractor_4bits_nice_1_z3),
    .D(selector_1bit_2to1_3_d));
  Selector_1bit_2to1 selector_1bit_2to1_4 (
    .Control(subtractor_4bits_nice_1_sign), .D1(subtractor_4bits_nice_2_z2), .D0(subtractor_4bits_nice_1_z2),
    .D(selector_1bit_2to1_4_d));
  Selector_1bit_2to1 selector_1bit_2to1_5 (
    .Control(subtractor_4bits_nice_1_sign), .D1(subtractor_4bits_nice_2_z1), .D0(subtractor_4bits_nice_1_z1),
    .D(selector_1bit_2to1_5_d));
  Selector_1bit_2to1 selector_1bit_2to1_6 (
    .Control(subtractor_4bits_nice_1_sign), .D1(subtractor_4bits_nice_2_z0), .D0(subtractor_4bits_nice_1_z0),
    .D(selector_1bit_2to1_6_d));
  or or_1 (Z3, selector_1bit_2to1_3_d, fa_4bits_1_z3);
  or or_2 (Z2, selector_1bit_2to1_4_d, fa_4bits_1_z2);
  or or_3 (Z1, selector_1bit_2to1_5_d, fa_4bits_1_z1);
  or or_4 (Z0, selector_1bit_2to1_6_d, fa_4bits_1_z0);
endmodule
