// Logisim project Counter_16max.circ as structural Verilog: 8 circuits, main circuit main
module main (
  input  in_1,
  input  in_2,
  input  in_3,
  input  in_4
);

  wire fa_4bits_1_s0, fa_4bits_1_s1, fa_4bits_1_s2, fa_4bits_1_s3, register_4bits_1_q0, register_4bits_1_q1,
       register_4bits_1_q2, register_4bits_1_q3;

  FA_4bits fa_4bits_1 (
    .B0(register_4bits_1_q0), .A0(in_1), .B1(register_4bits_1_q1), .B2(register_4bits_1_q2),
    .B3(register_4bits_1_q3), .S3(fa_4bits_1_s3), .S2(fa_4bits_1_s2), .S1(fa_4bits_1_s1), .S0(fa_4bits_1_s0));  // open: A1, A2, A3
  Register_4bits register_4bits_1 (
    .D3(fa_4bits_1_s3), .D2(fa_4bits_1_s2), .D1(fa_4bits_1_s1), .D0(fa_4bits_1_s0), .Clk(in_2), .EN(in_3),
    .R(in_4), .Q3(register_4bits_1_q3), .Q2(register_4bits_1_q2), .Q1(register_4bits_1_q1),
    .Q0(register_4bits_1_q0));
endmodule

module D_latch (
  input  D,
  input  Re0,
  input  WE,
  output Q,
  output Q1
);

  wire and_1_out, and_2_out, not_1_out, or_1_out, or_2_out;

  or or_1 (or_1_out, Re0, D);
  or or_2 (or_2_out, Re0, WE);
  not not_1 (not_1_out, or_1_out);
  and and_1 (and_1_out, or_1_out, or_2_out);
  and and_2 (and_2_out, or_2_out, not_1_out);
  nor nor_1 (Q, and_1_out, Q1);
  nor nor_2 (Q1, Q, and_2_out);
endmodule

module D_flip_flop (
  input  D,
  input  EN,
  input  R,
  input  Clk,
  output Q
);

  wire and_1_out, and_2_out, d_latch_1_q, not_1_out, or_1_out, or_2_out;

  and and_1 (and_1_out, D, EN);
  and and_2 (and_2_out, EN, Clk);
  not not_1 (not_1_out, and_2_out);
  D_latch d_latch_1 (.D(and_1_out), .WE(not_1_out), .Q(d_latch_1_q));  // open: Re0, Q1
  or or_1 (or_1_out, R, d_latch_1_q);
  or or_2 (or_2_out, R, Clk);
  D_latch d_latch_2 (.D(or_1_out), .WE(or_2_out), .Q(Q));  // open: Re0, Q1
endmodule

module Register_4bits (
  input  D3,
  input  D2,
  input  D1,
  input  D0,
  input  Clk,
  input  EN,
  input  R,
  output Q3,
  output Q2,
  output Q1,
  output Q0
);

  D_flip_flop d_flip_flop_1 (.D(D3), .EN(EN), .R(R), .Clk(Clk), .Q(Q3));
  D_flip_flop d_flip_flop_2 (.D(D2), .EN(EN), .R(R), .Clk(Clk), .Q(Q2));
  D_flip_flop d_flip_flop_3 (.D(D1), .EN(EN), .R(R), .Clk(Clk), .Q(Q1));
  D_flip_flop d_flip_flop_4 (.D(D0), .EN(EN), .R(R), .Clk(Clk), .Q(Q0));
endmodule

module HA (
  input  B,
  input  A,
  output S,
  output Cout
);

  xor xor_1 (S, B, A);
  and and_1 (Cout, B, A);
endmodule

module FA (
  input  Cin,
  input  B,
  input  A,
  output S,
  output Cout
);

  wire ha_1_cout, ha_1_s, ha_2_cout;

  HA ha_1 (.B(B), .A(A), .S(ha_1_s), .Cout(ha_1_cout));
  HA ha_2 (.B(Cin), .A(ha_1_s), .S(S), .Cout(ha_2_cout));
  or or_1 (Cout, ha_2_cout, ha_1_cout);
endmodule

module FA_4bits (
  input  B0,
  input  A0,
  input  B1,
  input  A1,
  input  B2,
  input  A2,
  input  B3,
  input  A3,
  output S3,
  output S2,
  output S1,
  output S0
);

  wire fa_1_cout, fa_2_cout, fa_3_cout, fa_4_cout;

  FA fa_1 (.B(B0), .A(A0), .S(S0), .Cout(fa_1_cout));  // open: Cin
  LED led_1 (.in(fa_1_cout));
  FA fa_2 (.Cin(fa_1_cout), .B(B1), .A(A1), .S(S1), .Cout(fa_2_cout));
  LED led_2 (.in(fa_2_cout));
  FA fa_3 (.Cin(fa_2_cout), .B(B2), .A(A2), .S(S2), .Cout(fa_3_cout));
  LED led_3 (.in(fa_3_cout));
  FA fa_4 (.Cin(fa_3_cout), .B(B3), .A(A3), .S(S3), .Cout(fa_4_cout));
  LED led_4 (.in(fa_4_cout));
  // OR_Gate a is placed but not wired
endmodule

module Selector (
  input  Control,
  input  D1,
  input  D0,
  output D
);

  wire and_1_out, and_2_out;

  and and_1 (and_1_out, D1, Control);
  and and_2 (and_2_out, ~Control, D0);  // AND_Gate
  or or_1 (D, and_1_out, and_2_out);
endmodule
