// Logisim project D_Latch_Reset.circ as structural Verilog: 1 circuit, main circuit main
module main (
  input  in_1,
  input  WE,
  input  in_3,
  output out_4,
  output out_5
);

  wire and_1_out, and_2_out, not_1_out, or_1_out, or_2_out;

  or or_1 (or_1_out, in_1, in_3);
  or or_2 (or_2_out, in_1, WE);
  not not_1 (not_1_out, or_1_out);
  and and_1 (and_1_out, or_1_out, or_2_out);
  and and_2 (and_2_out, or_2_out, not_1_out);
  nor nor_1 (out_4, and_1_out, out_5);
  nor nor_2 (out_5, out_4, and_2_out);
endmodule
