// Logisim project D_flip_flop_withENABLE.circ as structural Verilog: 3 circuits, main circuit main
module main (
  input  D,
  input  EN,
  output out_3
);

  wire and_1_out, and_2_out, Clk_out, d_latch_1_q, not_1_out;

  Button Clk (.out(Clk_out));
  and and_1 (and_1_out, D, EN);
  and and_2 (and_2_out, EN, Clk_out);
  not not_1 (not_1_out, and_2_out);
  D_latch d_latch_1 (.D(and_1_out), .WE(not_1_out), .Q(d_latch_1_q));  // open: Re0, Q1
  D_latch d_latch_2 (.D(d_latch_1_q), .WE(Clk_out), .Q(out_3));  // open: Re0, Q1
endmodule

module D_latch (
  input  D,
  input  Re0,
  input  WE,
  output Q,
  output Q1
);

  wire and_1_out, and_2_out, not_1_out, or_1_out, or_2_out;

  or or_1 (or_1_out, Re0, D);
  or or_2 (or_2_out, Re0, WE);
  not not_1 (not_1_out, or_1_out);
  and and_1 (and_1_out, or_1_out, or_2_out);
  and and_2 (and_2_out, or_2_out, not_1_out);
  nor nor_1 (Q, and_1_out, Q1);
  nor nor_2 (Q1, Q, and_2_out);
endmodule

module D_flip_flop (
  input  D,
  input  EN,
  output out_3
);

  wire and_1_out, and_2_out, Clk_out, d_latch_1_q, not_1_out;

  Button Clk (.out(Clk_out));
  and and_1 (and_1_out, D, EN);
  and and_2 (and_2_out, EN, Clk_out);
  not not_1 (not_1_out, and_2_out);
  D_latch d_latch_1 (.D(and_1_out), .WE(not_1_out), .Q(d_latch_1_q));  // open: Re0, Q1
  D_latch d_latch_2 (.D(d_latch_1_q), .WE(Clk_out), .Q(out_3));  // open: Re0, Q1
endmodule
