// Logisim project Register_4bits.circ as structural Verilog: 4 circuits, main circuit main
module main (
  input  D3,
  input  D2,
  input  D1,
  input  D0,
  input  EN,
  input  R
);

  wire button_1_out;

  Button button_1 (.out(button_1_out));
  Register_4bits register_4bits_1 ();  // open: D3, D2, D1, D0, Clk, EN, R
  D_flip_flop d_flip_flop_1 (.D(D3), .EN(EN), .R(R), .Clk(button_1_out));  // open: Q
  D_flip_flop d_flip_flop_2 (.D(D2), .EN(EN), .R(R), .Clk(button_1_out));  // open: Q
  D_flip_flop d_flip_flop_3 (.D(D1), .EN(EN), .R(R), .Clk(button_1_out));  // open: Q
  // D_flip_flop d_flip_flop_4: pin names not known; wires that end beside it: EN, R, button_1_out, D0
endmodule

module D_latch (
  input  D,
  input  Re0,
  input  WE,
  output Q,
  output Q1
);

  wire and_1_out, and_2_out, not_1_out, or_1_out, or_2_out;

  or or_1 (or_1_out, Re0, D);
  or or_2 (or_2_out, Re0, WE);
  not not_1 (not_1_out, or_1_out);
  and and_1 (and_1_out, or_1_out, or_2_out);
  and and_2 (and_2_out, or_2_out, not_1_out);
  nor nor_1 (Q, and_1_out, Q1);
  nor nor_2 (Q1, Q, and_2_out);
endmodule

module D_flip_flop (
  input  D,
  input  EN,
  input  R,
  input  Clk,
  output Q
);

  wire and_1_out, and_2_out, d_latch_1_q, not_1_out, or_1_out, or_2_out;

  and and_1 (and_1_out, D, EN);
  and and_2 (and_2_out, EN, Clk);
  not not_1 (not_1_out, and_2_out);
  D_latch d_latch_1 (.D(and_1_out), .WE(not_1_out), .Q(d_latch_1_q));  // open: Re0, Q1
  or or_1 (or_1_out, R, d_latch_1_q);
  or or_2 (or_2_out, R, Clk);
  D_latch d_latch_2 (.D(or_1_out), .WE(or_2_out), .Q(Q));  // open: Re0, Q1
endmodule

module Register_4bits (
  input  D3,
  input  D2,
  input  D1,
  input  D0,
  input  Clk,
  input  EN,
  input  R
);

  D_flip_flop d_flip_flop_1 (.D(D3), .EN(EN), .R(R), .Clk(Clk));  // open: Q
  D_flip_flop d_flip_flop_2 (.D(D2), .EN(EN), .R(R), .Clk(Clk));  // open: Q
  D_flip_flop d_flip_flop_3 (.D(D1), .EN(EN), .R(R), .Clk(Clk));  // open: Q
  // D_flip_flop d_flip_flop_4: pin names not known; wires that end beside it: EN, R, Clk, D0
endmodule
