// Logisim project XOR.circ as structural Verilog: 1 circuit, main circuit main
module main (
  input  A1,
  input  B1,
  output out_3
);

  wire and_1_out, and_2_out, not_1_out, not_2_out;

  not not_1 (not_1_out, B1);
  not not_2 (not_2_out, A1);
  and and_1 (and_1_out, A1, not_1_out);
  and and_2 (and_2_out, not_2_out, B1);
  or or_1 (out_3, and_1_out, and_2_out);
endmodule
